# Fritzing sketch gesture-glove (saved by Fritzing 1.0.6)

parts:
  RF1 = DIY Velostat flex strip
  R1 = divider resistor [resistance=10k]
  C1 = filter capacitor [capacitance=100nF]
  RF2 = DIY Velostat flex strip
  R2 = divider resistor [resistance=10k]
  C2 = filter capacitor [capacitance=100nF]
  RF3 = DIY Velostat flex strip
  R3 = divider resistor [resistance=10k]
  C3 = filter capacitor [capacitance=100nF]
  RF4 = DIY Velostat flex strip
  R4 = divider resistor [resistance=10k]
  C4 = filter capacitor [capacitance=100nF]
  RF5 = DIY Velostat flex strip
  R5 = divider resistor [resistance=10k]
  C5 = filter capacitor [capacitance=100nF]
  U1 = Adafruit ESP32-S3 Feather [part_number="Adafruit #5323"]
  U2 = InvenSense MPU6050
  BT1 = LiPo 3.7V 500mAh
  SW6 = Slide switch: EN to GND
  P1 = Conductive fingertip pad
  P2 = Conductive fingertip pad
  P3 = Conductive fingertip pad
  P4 = Conductive fingertip pad
  P5 = Conductive fingertip pad
  PALM = Common conductive palm fabric
  NOTES = Glove diagram annotations  # not connected

nets:
  3V3: RF1.3V3, RF2.3V3, RF3.3V3, RF4.3V3, RF5.3V3, U1.3.3V, U2.VCC
  N1: RF1.Signal, R1.Signal, C1.Signal, U1.A5
  GND: R1.GND, C1.GND, R2.GND, C2.GND, R3.GND, C3.GND, R4.GND, C4.GND, R5.GND, C5.GND, U1.GND, U2.GND, U2.AD0, BT1.GND, SW6.GND, PALM.GND
  N2: RF2.Signal, R2.Signal, C2.Signal, U1.D5
  N3: RF3.Signal, R3.Signal, C3.Signal, U1.D6
  N4: RF4.Signal, R4.Signal, C4.Signal, U1.D9
  N5: RF5.Signal, R5.Signal, C5.Signal, U1.D10
  N6: U1.A4, P5.Contact
  N7: U1.A3, P4.Contact
  N8: U1.A2, P3.Contact
  N9: U1.A1, P2.Contact
  N10: U1.A0, P1.Contact
  N11: U1.EN, SW6.EN
  N12: U1.SCL, U2.SCL
  N13: U1.SDA, U2.SDA
  N14: U1.VBAT, BT1.VBAT

custom parts:
  DIY Velostat flex strip: Conceptual glove harness part. Dimensions and PCB view are illustrative.
  10 kohm divider resistor: Conceptual glove harness part. Dimensions and PCB view are illustrative.
  100 nF filter capacitor: Conceptual glove harness part. Dimensions and PCB view are illustrative.
  Adafruit ESP32-S3 Feather: The ESP32-S3 has arrived in Feather format - and what a great way to get started with this powerful new chip from Espressif! With dual 240 MHz cores, WiFi and BLE support, and native USB, this Feather is great for powering your IoT projects. That's right - it's the new Adafruit ESP32-S3 Feather! With native USB and 8 MB flash, this board will let you upgrade your existing ESP32 projects.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
  LiPo 3.7V 500mAh: Conceptual glove harness part. Dimensions and PCB view are illustrative.
  Slide switch: EN to GND: Conceptual glove harness part. Dimensions and PCB view are illustrative.
  Conductive fingertip pad: Conceptual glove harness part. Dimensions and PCB view are illustrative.
  Common conductive palm fabric: Conceptual glove harness part. Dimensions and PCB view are illustrative.
  Glove diagram annotations: Conceptual glove harness part. Dimensions and PCB view are illustrative.
